# Fritzing sketch circuit diagram (saved by Fritzing 0.9.4)

parts:
  U1 = ESP32-38PinWide [part_number=ESP32-38PinWide]
  DHT1 = Humidity and Temperature Sensor DHT11
  Part1 = FC-28 Soil Hygrometer Module
  Part2 = MQ-7 breakout
  e-radionica_com1 = LM393 LDR breakout [part_number=100027]

nets:
  VCC: U1.3.3, DHT1.Vcc, Part1.VCC, Part2.VCC, e-radionica_com1.VCC
  N1: U1.GPIO26, Part1.AO
  N2: U1.GPIO27, DHT1.Data-signal
  N3: U1.GPIO12, Part2.AO
  GND: U1.GND, DHT1.GND_2, e-radionica_com1.GND
  N4: U1.GPIO13, e-radionica_com1.AO
  GND_2: Part1.GND, Part2.GND

custom parts:
  ESP32-38PinWide: Generic 38-Pin ESP32 with wide format (only access to one side of pins on a breadboard) based on Stephen Lilley's HiLetgo ESP-WROOM-32 ESP32 ESP-32S Development Board.
  Humidity and Temperature Sensor DHT11: Digital relative humidity & temperature sensor DHT11
  FC-28 Soil Hygrometer Module: The FC-28 is a soil hygrometer module that uses the Texas Instruments LM393 comparator chip to provide an analog measurement of soil humidity. The digital output is high when soil moisture is over a certain threshold, as determined by adjusting the potentiometer.
  MQ-7 breakout: SKU: 101282
